# Fritzing sketch diagrama_simonTroni_byDavidRoniHernandezBeltran (saved by Fritzing 0.9.3b)
circuit board: 8.46667cm x 5.64444cm
breadboards: 1

parts:
  Componente1 = Arduino Uno (Rev3)
  S1 = Pushbutton [package=THT]
  LED1 = LED - 5mm [color="Blue (430nm)" package="5 mm [THT]"]
  LED2 = LED - 5mm [color="Red (633nm)" package="5 mm [THT]"]
  S2 = Pushbutton [package=THT]
  S3 = Pushbutton [package=THT]
  S4 = Pushbutton [package=THT]
  LED4 = LED - 5mm [color="Yellow (595nm)" package="5 mm [THT]"]
  LED3 = smd LED [color="Green (555nm)" package="1206 [SMD]"]
  R1 = Resistor [tolerance=±5% resistance=220 package=THT]
  R2 = Resistor [tolerance=±5% resistance=220 package=THT]
  R3 = Resistor [tolerance=±5% resistance=220 package=THT]
  R4 = Resistor [tolerance=±5% resistance=220 package=THT]
  R5 = Resistor [tolerance=±5% resistance=220 package=THT]
  R6 = Rotary Potentiometer (Small) [maximum_resistance=5kΩ package=THT]
  J1 = Piezo Speaker

nets:
  N1: Componente1.D8, S1.leg1
  N2: Componente1.D9_PWM, LED1.cathode
  N3: Componente1.D11_PWM/MOSI, J1.pin2
  N4: Componente1.GND, S1.leg0, S2.leg0, S3.leg0, S4.leg0, R1.Pin_0, R2.Pin_0, R3.Pin_0, R4.Pin_0, R6.wiper
  N5: Componente1.D3_PWM, LED4.cathode
  N6: Componente1.D4, S3.leg1
  N7: Componente1.D5_PWM, LED3.cathode
  N8: Componente1.D6_PWM, S2.leg1
  N9: Componente1.D7, LED2.cathode
  N10: LED1.anode, R4.Pin_1
  N11: LED2.anode, R3.Pin_1
  N12: LED4.anode, R1.Pin_1
  N13: LED3.anode, R2.Pin_1
  N14: R5.Pin_0, J1.pin1
  N15: R5.Pin_1, R6.leg2

notes:
  22[Ω]
  Potenciometro
  de 5[kΩ]
  Las resistencias de los leds pueden ser de 220[Ω] o 330[Ω]
  Observación:
  A) Anodo de led(patita mas larga) va conectado a los pines del arduino.
  B) Catodo de led(patita mas pequeña) va conectado al GND de arduino.
